// Logisim project F3_light.circ as structural Verilog: 1 circuit, main circuit main
module main (
  input  A,
  input  B,
  input  C,
  input  D
);

  wire AB_out, ABnCnDn_out, AC_out, AD_out, AfeiD_out, AnB_out, AnBCn_out, AnBCnD_out, AnBD_out, AnBDn_out,
       AnBn_out, AnBnC_out, AnC_out, AnCD_out, AnCDn_out, AnCnDn_out, BnCnDn_out, not_1_out, not_2_out,
       not_3_out, not_4_out, Y0_out, Y1_out, Y2_out, Y3_out, Y4_out, Y5_out, Y6_out, Y7_out;

  not not_1 (not_1_out, A);
  not not_2 (not_2_out, B);
  not not_3 (not_3_out, C);
  not not_4 (not_4_out, D);
  and AnBnC (AnBnC_out, not_1_out, not_2_out, C);
  and AnBCn (AnBCn_out, not_1_out, B, not_3_out);
  and AnCDn (AnCDn_out, not_1_out, C, not_4_out);
  and ABnCnDn (ABnCnDn_out, not_2_out, A, not_3_out, not_4_out);
  and AnBDn (AnBDn_out, not_1_out, B, not_4_out);
  and BnCnDn (BnCnDn_out, not_2_out, not_3_out, not_4_out);
  and AnBD (AnBD_out, not_1_out, B, D);
  and AnC (AnC_out, not_1_out, C);
  and AnBn (AnBn_out, not_1_out, not_2_out);
  and AnCnDn (AnCnDn_out, not_1_out, not_3_out, not_4_out);
  and AnCD (AnCD_out, not_1_out, C, D);
  and AnBCnD (AnBCnD_out, not_1_out, B, not_3_out, D);
  and AnB (AnB_out, not_1_out, B);
  and AfeiD (AfeiD_out, not_1_out, D);
  and AB (AB_out, A, B);
  and AC (AC_out, A, C);
  and AD (AD_out, A, D);
  or Y0 (Y0_out, AnBnC_out, AnBCn_out, AnCDn_out, ABnCnDn_out);
  or Y1 (Y1_out, AnBCn_out, AnBDn_out, BnCnDn_out);
  or Y2 (Y2_out, AnBD_out, AnC_out, BnCnDn_out);
  or Y3 (Y3_out, AnBn_out, AnCnDn_out, AnCD_out, BnCnDn_out);
  or Y4 (Y4_out, AnCDn_out, BnCnDn_out);
  or Y5 (Y5_out, AnBnC_out, AnBCnD_out, AnCDn_out, BnCnDn_out);
  or Y6 (Y6_out, AnB_out, AfeiD_out, BnCnDn_out);
  or Y7 (Y7_out, AB_out, AC_out, AD_out);
  _7_Segment_Display u_7_segment_display_1 (
    .g(Y0_out), .f(Y1_out), .a(Y2_out), .b(Y3_out), .e(Y4_out), .d(Y5_out), .c(Y6_out), .dp(Y7_out));
endmodule
